# Fritzing sketch e02_wiring_v2 (saved by Fritzing 0.9.9b)

parts:
  MH-ET_LIVE_ESP32_DEVKIT1 = MH-ET LIVE ESP32 DEVKIT 38 pins
  Grove1 = Grove OLED 128x96
  microSD1 = MicroSD Card Module
  RHT1 = Humidity and Temperature Sensor RHT03
  U1 = ESP32S-HiLetgo [part_number=ESP32S-HiLetgo]  # not connected

nets:
  VCC: MH-ET_LIVE_ESP32_DEVKIT1.3V3, Grove1.VCC, RHT1.Vcc
  N1: MH-ET_LIVE_ESP32_DEVKIT1.IO25, Grove1.SCL
  N2: MH-ET_LIVE_ESP32_DEVKIT1.IO26, Grove1.SDA
  N3: MH-ET_LIVE_ESP32_DEVKIT1.GND#58, RHT1.GND_2
  5V: MH-ET_LIVE_ESP32_DEVKIT1.5V, microSD1.VCC
  GND: MH-ET_LIVE_ESP32_DEVKIT1.GND#64, Grove1.GND, microSD1.GND
  N4: MH-ET_LIVE_ESP32_DEVKIT1.IO23, microSD1.MOSI
  N5: MH-ET_LIVE_ESP32_DEVKIT1.IO19, microSD1.MISO
  N6: MH-ET_LIVE_ESP32_DEVKIT1.IO18, microSD1.SCK
  N7: MH-ET_LIVE_ESP32_DEVKIT1.IO5, microSD1.CS
  N8: MH-ET_LIVE_ESP32_DEVKIT1.IO4, RHT1.Data-signal

notes:
  esp32-02 (e02)
  DHT22
  OLED - Pin order different - SCL/SDA swapped
  microSD module
  Pin order same:
  CS, SCK, MOSI, MISO, VCC, GND
  ESP32
  pin order different

custom parts:
  MH-ET LIVE ESP32 DEVKIT 38 pins: http://mh.nodebb.com/topic/2/mh-et-live-esp32-devkit
  ESP32S-HiLetgo: HiLetgo ESP-WROOM-32 ESP32 ESP-32S Development Board 2.4GHz Dual-Mode WiFi + Bluetooth Dual Cores Microcontroller The ESP32 integrated with Antenna switches, RF Balun, power amplifiers, low-noise amplifiers, filters, and management modules, and the entire solution occupies the least area of PCB. 2.4 GHz Wi-Fi plus Bluetooth dual-mode chip, with TSMC Ultra-low power consumption 40nm technology,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
